// Logisim project cs240a1_p1.circ as structural Verilog: 1 circuit, main circuit main
module main (
  input  a,
  input  b,
  input  c,
  input  d,
  output f
);

  wire and_1_out, and_2_out, and_3_out, and_4_out, not_1_out, not_2_out, not_3_out;

  not not_1 (not_1_out, a);
  not not_2 (not_2_out, c);
  not not_3 (not_3_out, d);
  and and_1 (and_1_out, not_1_out, b, c);
  and and_2 (and_2_out, not_1_out, d);
  and and_3 (and_3_out, b, d);
  and and_4 (and_4_out, not_3_out, not_2_out, not_2_out, a);
  or or_1 (f, and_1_out, and_2_out, and_3_out, and_4_out);
endmodule
