// Logisim project cs240a1_p2.circ as structural Verilog: 1 circuit, main circuit main
module main (
  input  x0,
  input  x1,
  input  y0,
  input  y1,
  output z0,
  output z1
);

  wire and_1_out, and_2_out, and_3_out, not_1_out, not_2_out;

  not not_1 (not_1_out, x1);
  not not_2 (not_2_out, y1);
  and and_1 (and_1_out, x0, y0);
  and and_2 (and_2_out, not_1_out, x0, y1);
  and and_3 (and_3_out, y0, x1, not_2_out);
  or or_1 (z0, and_1_out, and_2_out, and_3_out);
  and and_4 (z1, y1, x1);
endmodule
