// Logisim project cs240a1_p3.circ as structural Verilog: 1 circuit, main circuit main
module main (
  input  in_1,
  input  [7:0] start_count,
  input  in_3,
  output alarm,
  output [7:0] current_count
);

  wire clock_1_out, not_1_out, not_2_out;
  wire [7:0] adder_1_out, bit_extender_1_out, bit_extender_2_out, register_1_q;

  assign bit_extender_1_out = {{7{1'b0}}, in_1};  // Bit_Extender bit_extender_1
  Subtractor subtractor_1 (.a(start_count), .b(register_1_q), .out(current_count));  // open: bin, bout
  Register register_1 (.D(adder_1_out), .en(not_2_out), .Q(register_1_q), .clk(clock_1_out));  // open: clr
  Clock clock_1 (.out(clock_1_out));
  not not_1 (not_1_out, in_3);
  Comparator comparator_1 (.a(bit_extender_1_out), .b(current_count), .eq(alarm));  // open: gt, lt
  Adder adder_1 (.a(register_1_q), .b(bit_extender_2_out), .out(adder_1_out));  // open: cin, cout
  assign bit_extender_2_out = {{7{1'b0}}, not_1_out};  // Bit_Extender bit_extender_2
  not not_2 (not_2_out, alarm);
endmodule
